// Logisim project mux.circ as structural Verilog: 1 circuit, main circuit main
module main (
  input  in_1,
  input  in_2
);

  wire and_1_out, and_2_out, and_3_out, not_1_out, not_2_out, or_1_out;

  not not_1 (not_1_out, in_1);
  or or_1 (or_1_out, and_3_out, and_1_out);
  and and_1 (and_1_out, in_2, in_1);
  not not_2 (not_2_out, and_2_out);
  and and_2 (and_2_out, in_2, not_1_out);
  and and_3 (and_3_out, or_1_out, not_2_out);
  LED led_1 (.in(and_3_out));
endmodule
