// Logisim project ADDER2.circ as structural Verilog: 3 circuits, main circuit ADDR
module main (
  input  in_1,
  input  in_2,
  input  in_3,
  input  in_4
);

  wire aa_1_out_5, aa_1_out_6, aa_1_out_7, aa_1_out_8;

  LED led_1 (.in(aa_1_out_7));
  LED led_2 (.in(aa_1_out_8));
  LED led_3 (.in(aa_1_out_5));
  LED led_4 (.in(aa_1_out_6));
  AA aa_1 (
    .in_2(in_2), .out_7(aa_1_out_7), .in_1(in_1), .out_5(aa_1_out_5), .out_8(aa_1_out_8), .in_4(in_4),
    .out_6(aa_1_out_6), .in_3(in_3));
endmodule

module ADDR (
  input  A,
  input  B,
  input  C,
  output R,
  output CO
);

  wire and_1_out, and_2_out, xor_1_out;

  xor xor_1 (xor_1_out, A, B);
  and and_1 (and_1_out, xor_1_out, C);
  and and_2 (and_2_out, A, B);
  xor xor_2 (R, xor_1_out, C);
  or or_1 (CO, and_1_out, and_2_out);
endmodule

module AA (
  input  in_1,
  input  in_2,
  input  in_3,
  input  in_4,
  output out_5,
  output out_6,
  output out_7,
  output out_8
);


  assign out_5 = in_1;
  assign out_6 = in_3;
  assign out_7 = in_2;
  assign out_8 = in_4;
endmodule
