// Logisim project SIMPLE.circ as structural Verilog: 1 circuit, main circuit main
module main (
  input  A,
  input  B
);

  wire and_1_out, not_1_out, or_1_out;

  or or_1 (or_1_out, A, and_1_out);
  and and_1 (and_1_out, or_1_out, not_1_out);
  not not_1 (not_1_out, B);
  LED led_1 (.in(or_1_out));
endmodule
