// Logisim project example0.circ as structural Verilog: 1 circuit, main circuit main
module main (
  input  in_1,
  input  in_2
);

  LED led_1 (.in(in_1));

  assign in_2 = in_1;
endmodule
