// Logisim project test.circ as structural Verilog: 1 circuit, main circuit main
module main (
  input  in_1,
  input  in_2,
  input  in_3,
  input  in_4
);

  LED led_1 (.in(in_1));
  LED led_2 (.in(in_3));
  // NAND_Gate nand_1 has open pins: in0=in_1, out=open

  assign in_4 = in_3;
endmodule
